# Fritzing sketch ioThing-fritzing (saved by Fritzing 0.9.3b)
breadboards: 1

parts:
  Part1 = Photon
  S1 = Pushbutton [package="[THT]"]
  R2 = Rotary Potentiometer (Small) [maximum_resistance=100kΩ package=THT]
  LED1 = RGB LED - (4 legs) [package="5 mm [THT]"]
  T1 = TMP36 Temperature Sensor [package="TO92 [THT]"]
  R3 = Photocell (LDR) [package=THT]
  R4 = Resistor [tolerance=±5% resistance=10k package=THT]
  J1 = Piezo Speaker

nets:
  N1: Part1.A0, R2.wiper
  N2: Part1.A1, T1.Vout
  N3: Part1.A2, R3.pin_1, R4.Pin_0
  GND: Part1.GND, S1.Pin_1, S1.Pin_2, R2.leg1, LED1.green_cathode, T1.GND, R4.Pin_1, J1.pin1
  N4: Part1.D0, LED1.red_cathode
  N5: Part1.D1, S1.Pin_3, S1.Pin_4
  N6: Part1.D2, J1.pin2
  N7: Part1.3V3, R2.leg2, LED1.common_anode, T1.+Vs, R3.pin_0
